// Logisim project Circuito.circ as structural Verilog: 1 circuit, main circuit Contador Arbitrario
module Contador_Arbitrario (
);

  wire and_1_out, and_2_out, and_3_out, and_4_out, and_5_out, and_6_out, and_7_out, and_8_out, and_9_out,
       and_10_out, and_11_out, and_12_out, and_13_out, and_14_out, and_15_out, and_16_out, and_17_out,
       and_18_out, clock_1_out, JK0_q, JK0_qn, JK1_q, JK1_qn, JK2_q, JK2_qn, JK3_q, JK3_qn, or_1_out,
       or_2_out, or_3_out, or_4_out, or_5_out, or_6_out, or_7_out, or_8_out;

  Clock clock_1 (.out(clock_1_out));
  and and_1 (and_1_out, JK1_q, JK3_qn);
  and and_2 (and_2_out, JK3_q, JK2_q);
  and and_3 (and_3_out, JK3_qn, JK2_qn);
  and and_4 (and_4_out, JK2_qn, JK1_qn);
  and and_5 (and_5_out, JK3_q, JK1_q);
  and and_6 (and_6_out, JK1_qn, JK3_qn);
  or or_1 (or_1_out, and_1_out, and_2_out, and_3_out);
  or or_2 (or_2_out, and_4_out, and_5_out, and_6_out);
  J_K_Flip_Flop JK0 (.J(or_1_out), .clk(clock_1_out), .K(or_2_out), .Q(JK0_q), .Qn(JK0_qn));  // open: preset, en, reset
  and and_7 (and_7_out, JK2_qn, JK0_q);
  and and_8 (and_8_out, JK0_qn, JK2_q);
  and and_9 (and_9_out, JK0_q, JK3_q);
  and and_10 (and_10_out, JK0_qn, JK3_qn);
  or or_3 (or_3_out, and_10_out, JK2_q);
  or or_4 (or_4_out, and_7_out, and_8_out, and_9_out);
  J_K_Flip_Flop JK1 (.J(or_3_out), .clk(clock_1_out), .K(or_4_out), .Q(JK1_q), .Qn(JK1_qn));  // open: preset, en, reset
  and and_11 (and_11_out, JK3_qn, JK1_q, JK0_q);
  or or_5 (or_5_out, and_11_out, and_12_out);
  and and_12 (and_12_out, JK3_q, JK1_qn, JK0_qn);
  and and_13 (and_13_out, JK1_q, JK0_q);
  or or_6 (or_6_out, and_13_out, and_14_out);
  and and_14 (and_14_out, JK0_qn, JK3_q);
  J_K_Flip_Flop JK2 (.J(or_5_out), .clk(clock_1_out), .K(or_6_out), .Q(JK2_q), .Qn(JK2_qn));  // open: preset, en, reset
  and and_15 (and_15_out, JK1_qn, JK2_q);
  and and_16 (and_16_out, JK0_qn, JK1_q, JK2_qn);
  and and_17 (and_17_out, JK0_qn, JK2_qn);
  and and_18 (and_18_out, JK1_qn, JK2_qn);
  or or_7 (or_7_out, and_15_out, and_16_out);
  or or_8 (or_8_out, and_17_out, and_18_out);
  J_K_Flip_Flop JK3 (.J(or_7_out), .clk(clock_1_out), .K(or_8_out), .Q(JK3_q), .Qn(JK3_qn));  // open: preset, en, reset

  // Notes on the sheet:
  //   Contador Arbitario
  //   10-2-11-8-4-14-9-0-3-5
  //   Pablo Jesús González Rubio
endmodule
